// Logisim project Real_Alu.circ as structural Verilog: 17 circuits, main circuit In_A AND In_B
module In_A_AND_In_B (
  input  [7:0] In_A,
  input  [7:0] In_B,
  output [7:0] Alu_out
);

  assign Alu_out = In_A & In_B;  // AND_Gate and_1, 8 bits wide
endmodule

module In_a_OR_In_B (
  input  [7:0] In_A,
  input  [7:0] In_B,
  output [7:0] Alu_Out
);

  assign Alu_Out = In_A | In_B;  // OR_Gate or_1, 8 bits wide
endmodule

module Not_In_B (
  input  [7:0] In_B,
  output [7:0] Alu_Out
);

  assign Alu_Out = ~In_B;  // NOT_Gate not_1, 8 bits wide
endmodule

module Shift_to_left (
  input  D0,
  input  D1,
  input  D2,
  input  D3,
  input  D4,
  input  D5,
  input  D6,
  input  D7,
  output S0,
  output S1,
  output S2,
  output S3,
  output S4,
  output S5,
  output S7,
  output S6
);

  wire and_1_out, and_4_out, and_5_out, and_8_out, and_11_out, and_14_out, x2, x3, x4, x5, x6, x7;

  and and_1 (and_1_out, D0, 1'b0);
  and and_2 (S0, 1'b1, D1);
  or or_1 (S1, and_1_out, x2);
  and and_3 (x5, 1'b1, D5);
  and and_4 (and_4_out, D5, 1'b0);
  or or_2 (S6, and_4_out, x7);
  and and_5 (and_5_out, D1, 1'b0);
  and and_6 (x2, 1'b1, D2);
  or or_3 (S2, and_5_out, x3);
  and and_7 (x6, 1'b1, D6);
  and and_8 (and_8_out, D2, 1'b0);
  or or_4 (S3, and_8_out, x4);
  and and_9 (S7, D6, 1'b0);
  and and_10 (x3, 1'b1, D3);
  and and_11 (and_11_out, D3, 1'b0);
  or or_5 (S4, and_11_out, x5);
  and and_12 (x7, D7, 1'b1);
  and and_13 (x4, 1'b1, D4);
  and and_14 (and_14_out, D4, 1'b0);
  or or_6 (S5, and_14_out, x6);

  // Other names for the same wires on the sheet: _0 = D0; _1 = D1; _2 = D2; _3 = D3; _4 = D4; _5 = D5; _6 = D6;
  //   _7 = D7
endmodule

module Shift_to_right (
  input  D0,
  input  D1,
  input  D2,
  input  D3,
  input  D4,
  input  D5,
  input  D6,
  input  D7,
  output S0,
  output S1,
  output S2,
  output S3,
  output S4,
  output S5,
  output S7,
  output S6
);

  wire and_1_out, and_3_out, and_5_out, and_8_out, and_11_out, and_14_out, x2, x3, x4, x5, x6, x7;

  and and_1 (and_1_out, D0, 1'b1);
  and and_2 (S0, 1'b0, D1);
  or or_1 (S1, and_1_out, x2);
  and and_3 (and_3_out, D5, 1'b1);
  and and_4 (x5, 1'b0, D5);
  or or_2 (S6, and_3_out, x7);
  and and_5 (and_5_out, D1, 1'b1);
  and and_6 (x2, 1'b0, D2);
  or or_3 (S2, and_5_out, x3);
  and and_7 (x6, 1'b0, D6);
  and and_8 (and_8_out, D2, 1'b1);
  or or_4 (S3, and_8_out, x4);
  and and_9 (S7, D6, 1'b1);
  and and_10 (x3, 1'b0, D3);
  and and_11 (and_11_out, D3, 1'b1);
  or or_5 (S4, and_11_out, x5);
  and and_12 (x7, D7, 1'b0);
  and and_13 (x4, 1'b0, D4);
  and and_14 (and_14_out, D4, 1'b1);
  or or_6 (S5, and_14_out, x6);

  // Other names for the same wires on the sheet: _0 = D0; _1 = D1; _2 = D2; _3 = D3; _4 = D4; _5 = D5; _6 = D6;
  //   _7 = D7
endmodule

module in_A_ADD_in_B (
  input  [7:0] A,
  input  [7:0] B,
  output C,
  output [7:0] S
);

  wire C1, full_adder_1_c1, full_adder_2_c1, full_adder_3_c1, full_adder_4_c1, full_adder_5_c1,
       half_adder_1_c;

  half_adder half_adder_1 (.S(S[0]), .C(half_adder_1_c), .A(A[0]), .B(B[0]));
  full_adder full_adder_1 (.S(S[4]), .C1(full_adder_1_c1), .C0(C1), .A(A[4]), .B(B[4]));
  full_adder full_adder_2 (.S(S[1]), .C1(full_adder_2_c1), .C0(half_adder_1_c), .A(A[1]), .B(B[1]));
  full_adder full_adder_3 (.S(S[5]), .C1(full_adder_3_c1), .C0(full_adder_1_c1), .A(A[5]), .B(B[5]));
  full_adder full_adder_4 (.S(S[2]), .C1(full_adder_4_c1), .C0(full_adder_2_c1), .A(A[2]), .B(B[2]));
  full_adder full_adder_5 (.S(S[6]), .C1(full_adder_5_c1), .C0(full_adder_3_c1), .A(A[6]), .B(B[6]));
  full_adder full_adder_6 (.S(S[3]), .C1(C1), .C0(full_adder_4_c1), .A(A[3]), .B(B[3]));
  full_adder full_adder_7 (.S(S[7]), .C1(C), .C0(full_adder_5_c1), .A(A[7]), .B(B[7]));

  // Other names for the same wires on the sheet: _0 = S[0]; _1 = S[1]; _2 = S[2]; _3 = S[3]; _4 = S[4]; _5 = S[5];
  //   _6 = S[6]; _7 = S[7]
endmodule

module half_adder (
  input  A,
  input  B,
  output S,
  output C
);

  xor xor_1 (S, B, A);
  and and_1 (C, B, A);
endmodule

module full_adder (
  input  C0,
  input  A,
  input  B,
  output S,
  output C1
);

  wire and_1_out, and_2_out, and_3_out, xor_1_out;

  xor xor_1 (xor_1_out, B, A);
  xor xor_2 (S, xor_1_out, C0);
  and and_1 (and_1_out, A, C0);
  and and_2 (and_2_out, B, A);
  and and_3 (and_3_out, B, C0);
  or or_1 (C1, and_1_out, and_2_out, and_3_out);
endmodule

module Half_Subtractor (
  input  A,
  input  B,
  output D,
  output B_2
);

  wire not_1_out;

  not not_1 (not_1_out, A);
  xor xor_1 (D, A, B);
  and and_1 (B_2, B, not_1_out);
endmodule

module Full_Subtractor (
  input  b0,
  input  A,
  input  B,
  output D,
  output B_2
);

  wire and_1_out, and_2_out, not_1_out, not_2_out, xor_1_out;

  not not_1 (not_1_out, A);
  xor xor_1 (xor_1_out, B, A);
  not not_2 (not_2_out, xor_1_out);
  and and_1 (and_1_out, B, not_1_out);
  xor xor_2 (D, xor_1_out, b0);
  and and_2 (and_2_out, b0, not_2_out);
  or or_1 (B_2, and_2_out, and_1_out);
endmodule

module In_A_SUB_In_B (
  input  [7:0] A,
  input  [7:0] B,
  output B_2,
  output [7:0] D
);

  wire b1, full_subtractor_1_b_2, full_subtractor_2_b_2, full_subtractor_3_b_2, full_subtractor_4_b_2,
       full_subtractor_5_b_2, half_subtractor_1_b_2;

  Half_Subtractor half_subtractor_1 (.D(D[0]), .B_2(half_subtractor_1_b_2), .A(A[0]), .B(B[0]));
  Full_Subtractor full_subtractor_1 (.D(D[4]), .B_2(full_subtractor_1_b_2), .b0(b1), .A(A[4]), .B(B[4]));
  Full_Subtractor full_subtractor_2 (
    .D(D[1]), .B_2(full_subtractor_2_b_2), .b0(half_subtractor_1_b_2), .A(A[1]), .B(B[1]));
  Full_Subtractor full_subtractor_3 (
    .D(D[5]), .B_2(full_subtractor_3_b_2), .b0(full_subtractor_1_b_2), .A(A[5]), .B(B[5]));
  Full_Subtractor full_subtractor_4 (
    .D(D[2]), .B_2(full_subtractor_4_b_2), .b0(full_subtractor_2_b_2), .A(A[2]), .B(B[2]));
  Full_Subtractor full_subtractor_5 (
    .D(D[6]), .B_2(full_subtractor_5_b_2), .b0(full_subtractor_3_b_2), .A(A[6]), .B(B[6]));
  Full_Subtractor full_subtractor_6 (.D(D[3]), .B_2(b1), .b0(full_subtractor_4_b_2), .A(A[3]), .B(B[3]));
  Full_Subtractor full_subtractor_7 (.D(D[7]), .B_2(B_2), .b0(full_subtractor_5_b_2), .A(A[7]), .B(B[7]));

  // Other names for the same wires on the sheet: _0 = D[0]; _1 = D[1]; _2 = D[2]; _3 = D[3]
endmodule

module INC_in_B (
  input  [7:0] B,
  output C,
  output [7:0] S
);

  wire C1, full_adder_1_c1, full_adder_2_c1, full_adder_3_c1, full_adder_4_c1, full_adder_5_c1,
       half_adder_1_c;

  half_adder half_adder_1 (.S(S[0]), .C(half_adder_1_c), .A(1'b1), .B(B[0]));
  full_adder full_adder_1 (.S(S[4]), .C1(full_adder_1_c1), .C0(C1), .A(1'b0), .B(B[4]));
  full_adder full_adder_2 (.S(S[1]), .C1(full_adder_2_c1), .C0(half_adder_1_c), .A(1'b0), .B(B[1]));
  full_adder full_adder_3 (.S(S[5]), .C1(full_adder_3_c1), .C0(full_adder_1_c1), .A(1'b0), .B(B[5]));
  full_adder full_adder_4 (.S(S[2]), .C1(full_adder_4_c1), .C0(full_adder_2_c1), .A(1'b0), .B(B[2]));
  full_adder full_adder_5 (.S(S[6]), .C1(full_adder_5_c1), .C0(full_adder_3_c1), .A(1'b0), .B(B[6]));
  full_adder full_adder_6 (.S(S[3]), .C1(C1), .C0(full_adder_4_c1), .A(1'b0), .B(B[3]));
  full_adder full_adder_7 (.S(S[7]), .C1(C), .C0(full_adder_5_c1), .A(1'b0), .B(B[7]));

  // Other names for the same wires on the sheet: _0 = S[0]; _1 = S[1]; _2 = S[2]; _3 = S[3]; _4 = S[4]; _5 = S[5];
  //   _6 = S[6]; _7 = S[7]
endmodule

module DEC_in_B (
  input  [7:0] B,
  output B_2,
  output [7:0] D
);

  wire b1, full_subtractor_1_b_2, full_subtractor_2_b_2, full_subtractor_3_b_2, full_subtractor_4_b_2,
       full_subtractor_5_b_2, half_subtractor_1_b_2;

  Half_Subtractor half_subtractor_1 (.D(D[0]), .B_2(half_subtractor_1_b_2), .A(B[0]), .B(1'b1));
  Full_Subtractor full_subtractor_1 (.D(D[4]), .B_2(full_subtractor_1_b_2), .b0(b1), .A(B[4]), .B(1'b0));
  Full_Subtractor full_subtractor_2 (
    .D(D[1]), .B_2(full_subtractor_2_b_2), .b0(half_subtractor_1_b_2), .A(B[1]), .B(1'b0));
  Full_Subtractor full_subtractor_3 (
    .D(D[5]), .B_2(full_subtractor_3_b_2), .b0(full_subtractor_1_b_2), .A(B[5]), .B(1'b0));
  Full_Subtractor full_subtractor_4 (
    .D(D[2]), .B_2(full_subtractor_4_b_2), .b0(full_subtractor_2_b_2), .A(B[2]), .B(1'b0));
  Full_Subtractor full_subtractor_5 (
    .D(D[6]), .B_2(full_subtractor_5_b_2), .b0(full_subtractor_3_b_2), .A(B[6]), .B(1'b0));
  Full_Subtractor full_subtractor_6 (.D(D[3]), .B_2(b1), .b0(full_subtractor_4_b_2), .A(B[3]), .B(1'b0));
  Full_Subtractor full_subtractor_7 (.D(D[7]), .B_2(B_2), .b0(full_subtractor_5_b_2), .A(B[7]), .B(1'b0));

  // Other names for the same wires on the sheet: _0 = D[0]; _1 = D[1]; _2 = D[2]; _3 = D[3]
endmodule

module RealAlu (
  input  E,
  input  [7:0] in_A,
  input  [7:0] in_B,
  input  [3:0] AluOp,
  output Z,
  output [7:0] out_6,
  output V,
  output Carry
);

  wire comparator_1_v, in_a_add_in_b_1_c, inc_in_b_1_c, or_1_out, z_1_x;
  wire [7:0] _0, _1, _2, _3, _4, _5, _6, _7, _8, bit_extender_1_out, multiplexer_1_out;

  Not_In_B not_in_b_1 (.In_B(in_B), .Alu_Out(_2));
  Shift_to_left shift_to_left_1 (
    .D0(in_B[0]), .D1(in_B[1]), .D2(in_B[2]), .D3(in_B[3]), .D4(in_B[4]), .D5(in_B[5]), .D6(in_B[6]),
    .D7(in_B[7]), .S0(_3[0]), .S1(_3[1]), .S6(_3[6]), .S2(_3[2]), .S7(_3[7]), .S3(_3[3]), .S4(_3[4]),
    .S5(_3[5]));
  in_A_ADD_in_B in_a_add_in_b_1 (.A(in_A), .B(in_B), .C(in_a_add_in_b_1_c), .S(_5));
  In_A_AND_In_B in_a_and_in_b_1 (.In_A(in_A), .In_B(in_B), .Alu_out(_0));
  In_a_OR_In_B in_a_or_in_b_1 (.In_A(in_A), .In_B(in_B), .Alu_Out(_1));
  Shift_to_right shift_to_right_1 (
    .D0(in_B[0]), .D1(in_B[1]), .D2(in_B[2]), .D3(in_B[3]), .D4(in_B[4]), .D5(in_B[5]), .D6(in_B[6]),
    .D7(in_B[7]), .S0(_4[0]), .S1(_4[1]), .S6(_4[6]), .S2(_4[2]), .S7(_4[7]), .S3(_4[3]), .S4(_4[4]),
    .S5(_4[5]));
  In_A_SUB_In_B in_a_sub_in_b_1 (.A(in_A), .B(in_B), .D(_6));  // open: B_2
  INC_in_B inc_in_b_1 (.B(in_B), .C(inc_in_b_1_c), .S(_7));
  Multiplexer #(.select(4), .width(8)) multiplexer_1 (
    .in0(_0), .in1(_1), .in2(_2), .in3(_3), .in4(_4), .in5(_5), .in6(_6), .in7(_7), .in8(_8), .in9(in_A),
    .in10({8{1'b0}}), .in11({8{1'b0}}), .in12({8{1'b0}}), .in13({8{1'b0}}), .in14({8{1'b0}}),
    .in15({8{1'b0}}), .out(multiplexer_1_out), .sel(AluOp), .en(E));
  or or_1 (or_1_out, inc_in_b_1_c, in_a_add_in_b_1_c);
  DEC_in_B dec_in_b_1 (.B(in_B), .D(_8));  // open: B_2
  and and_1 (Carry, or_1_out, E);
  and and_2 (Z, E, z_1_x);
  Z z_1 (
    .a(multiplexer_1_out[0]), .b(multiplexer_1_out[1]), .c(multiplexer_1_out[2]), .d(multiplexer_1_out[3]),
    .e(multiplexer_1_out[4]), .f(multiplexer_1_out[5]), .g(multiplexer_1_out[6]), .h(multiplexer_1_out[7]),
    .x(z_1_x));
  assign out_6 = multiplexer_1_out & bit_extender_1_out;  // AND_Gate and_3, 8 bits wide
  assign bit_extender_1_out = {{7{E}}, E};  // Bit_Extender bit_extender_1
  and and_4 (V, comparator_1_v, E);
  comparator comparator_1 (.V(comparator_1_v), .a(multiplexer_1_out));

  // Other names for the same wires on the sheet: _9[7:0] = in_A
endmodule

module comparator (
  input  [7:0] a,
  output V
);

  xor xor_1 (V, a[6], a[7]);
endmodule

module Z (
  input  a,
  input  b,
  input  c,
  input  d,
  input  e,
  input  f,
  input  g,
  input  h,
  output x
);

  wire not_1_out, not_2_out, not_3_out, not_4_out, not_5_out, not_6_out, not_7_out, not_8_out;

  not not_1 (not_1_out, a);
  not not_2 (not_2_out, b);
  not not_3 (not_3_out, c);
  not not_4 (not_4_out, d);
  not not_5 (not_5_out, e);
  not not_6 (not_6_out, f);
  not not_7 (not_7_out, g);
  not not_8 (not_8_out, h);
  and and_1 (x, not_1_out, not_2_out, not_3_out, not_4_out, not_5_out, not_6_out, not_7_out, not_8_out);
endmodule

module finish (
  input  [7:0] In_A,
  input  [7:0] In_B,
  input  [3:0] AluOp,
  input  EN,
  output [7:0] OUT,
  output OVERFLOW,
  output CARRY,
  output Z
);

  RealAlu realalu_1 (.in_A(In_A), .in_B(In_B), .AluOp(AluOp), .Carry(CARRY), .out_6(OUT), .V(OVERFLOW), .Z(Z), .E(EN));
endmodule
